// Digital circuit HazardUnit.dig as structural Verilog
module HazardUnit (
  input  [4:0] RR0_2,
  input  [4:0] RR1_1,
  input  [4:0] WR_3,
  input  RFW_3,
  input  [4:0] WR_4,
  input  RFW_4,
  output [1:0] FRD_0,
  output [1:0] FRD_1
);

  wire and_1_out, and_2_out, and_3_out, and_4_out, comparator_1_eq, comparator_2_eq, comparator_3_eq,
       comparator_4_eq, comparator_5_eq, comparator_6_eq, comparator_7_eq, comparator_8_eq;

  Comparator #(.Bits(5)) comparator_1 (.a(WR_3), .b(RR0_2), .eq(comparator_1_eq));  // open: gt, lt
  Comparator comparator_2 (.a(RFW_3), .b(1'b1), .eq(comparator_2_eq));  // open: gt, lt
  Comparator #(.Bits(5)) comparator_3 (.a(WR_4), .b(RR0_2), .eq(comparator_3_eq));  // open: gt, lt
  Comparator comparator_4 (.a(RFW_3), .b(1'b1), .eq(comparator_4_eq));  // open: gt, lt
  Comparator #(.Bits(5)) comparator_5 (.a(WR_3), .b(RR0_2), .eq(comparator_5_eq));  // open: gt, lt
  Comparator comparator_6 (.a(RFW_3), .b(1'b0), .eq(comparator_6_eq));  // open: gt, lt
  Comparator #(.Bits(5)) comparator_7 (.a(WR_4), .b(RR0_2), .eq(comparator_7_eq));  // open: gt, lt
  Comparator comparator_8 (.a(RFW_3), .b(1'b0), .eq(comparator_8_eq));  // open: gt, lt
  and and_1 (and_1_out, comparator_1_eq, comparator_2_eq);
  and and_2 (and_2_out, comparator_3_eq, comparator_4_eq);
  and and_3 (and_3_out, comparator_5_eq, comparator_6_eq);
  and and_4 (and_4_out, comparator_7_eq, comparator_8_eq);
  PriorityEncoder #(.Selector_Bits(2)) priorityencoder_1 (
    .in0(and_1_out), .in1(and_2_out), .in2(1'b0), .in3(1'b0), .num(FRD_0));  // open: any
  PriorityEncoder #(.Selector_Bits(2)) priorityencoder_2 (
    .in0(and_3_out), .in1(and_4_out), .in2(1'b0), .in3(1'b0), .num(FRD_1));  // open: any

  // Other names for the same wires on the sheet: RR0_1[4:0] = RR1_1
endmodule
